# Fritzing sketch CS355 (saved by Fritzing 0.9.3b)
breadboards: 1

parts:
  WeMos_D1_Mini_Relay_Shield_V2 = WeMos D1 Mini Relay Shield V2
  U1 = XR2206 [package=dil16]
  Part1 = Soil Moisture Sensor
  Part3 = Soil Moisture Sensor
  Raspberry_Pi_1 = Raspberry Pi 3 [part_number=RPI-3-V1.2]
  S1 = Tilt Switch [package=THT]
  WeMos_D1_Mini_Relay_Shield_V3 = WeMos D1 Mini Relay Shield V2
  WeMos_D1_Mini_Relay_Shield_V4 = WeMos D1 Mini Relay Shield V2
  L1 = Solenoid
  L2 = Solenoid
  M1 = DC Motor
  Power_plug1 = Power plug
  Power_plug2 = Power plug
  Power_plug3 = Power plug

nets:
  3V3: WeMos_D1_Mini_Relay_Shield_V2.3V3, WeMos_D1_Mini_Relay_Shield_V3.5V
  5V: WeMos_D1_Mini_Relay_Shield_V2.5V, U1.SYMA1, U1.SYMA2, Part1.VCC, Part3.VCC, Raspberry_Pi_1.3v3, Raspberry_Pi_1.5V, S1.Pin_1
  N1: WeMos_D1_Mini_Relay_Shield_V2.COM, M1.pin_1
  N2: WeMos_D1_Mini_Relay_Shield_V2.D8, WeMos_D1_Mini_Relay_Shield_V3.G
  GND: WeMos_D1_Mini_Relay_Shield_V2.G, U1.FSKI, U1.SYNCO, U1.WAVEA2, Part1.GND, Part3.GND, Raspberry_Pi_1.GND, Raspberry_Pi_1.GPIO19
  N3: WeMos_D1_Mini_Relay_Shield_V2.NO, Power_plug3.VCC
  N4: U1.AMSI, Part1.SIG
  N5: U1.STO, Part3.SIG
  N6: U1.BIAS, Raspberry_Pi_1.GPIO12
  N7: U1.GND, Raspberry_Pi_1.GPIO16
  N8: Raspberry_Pi_1.GPIO21, S1.Pin_2
  3V3_2: WeMos_D1_Mini_Relay_Shield_V3.3V3, WeMos_D1_Mini_Relay_Shield_V4.5V
  N9: WeMos_D1_Mini_Relay_Shield_V3.COM, L2.pin1
  N10: WeMos_D1_Mini_Relay_Shield_V3.D8, WeMos_D1_Mini_Relay_Shield_V4.G
  N11: WeMos_D1_Mini_Relay_Shield_V3.NO, Power_plug2.VCC
  N12: WeMos_D1_Mini_Relay_Shield_V4.COM, L1.pin1
  N13: WeMos_D1_Mini_Relay_Shield_V4.NO, Power_plug1.VCC
  N14: L1.pin2, Power_plug1.GND
  N15: L2.pin2, Power_plug2.GND
  N16: M1.pin_2, Power_plug3.GND

notes:
  Water Pump
  Solenoid Valve
  Water Level Float Switch
  5V Relays
  12V DC
  MCP3008 Analog to Digital Converter
  Water tube to plant A
  Water tube to plant B
  Water from reservoir to valves
